# Fritzing sketch Circuit (saved by Fritzing 1.0.4)
breadboards: 1

parts:
  Part1 = STM32F407G-DISC1
  Part2 = FTDI Basic Programmer
  Part3 = Barometric Pressure Sensor - BMP180 Breakout (GY-68)
  U1 = ESP32-38PinWide [part_number=ESP32-38PinWide]
  U2 = WS2812 RGB LED matrix 4x4
  OLED_I2C1 = OLED 128x64 I2C Monochrome Display

nets:
  N1: Part1.pin7, Part2.TXO
  N2: Part1.pin9, U2.DIN
  GND: Part1.pin12, Part1.pin25, Part1.pin26, Part1.pin50, Part1.pin51, Part1.pin76, Part3.GND, U1.GPIO11, U2.GND, OLED_I2C1.GND
  N3: Part1.pin32, Part2.RXI
  N4: Part1.pin62, Part3.SCL
  N5: Part1.pin69, U1.GPIO16
  N6: Part1.pin77, U2.VCC
  VCC: Part1.pin78, Part3.VCC, OLED_I2C1.VDD
  N7: Part1.pin85, Part3.SDA
  N8: Part1.pin94, U1.GPIO17

custom parts:
  STM32F407G-DISC1: The STM32F4DISCOVERY Discovery kit allows users to easily develop applications with the STM32F407VG high-performance microcontroller with the Arm® Cortex®-M4 32-bit core. It includes everything required either for beginners or experienced users to get started quickly. Based on STM32F407VG, it includes an ST-LINK/V2-A embedded debug tool, one STMEMS digital accelerometer, one digital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
  ESP32-38PinWide: Generic 38-Pin ESP32 with wide format (only access to one side of pins on a breadboard) based on Stephen Lilley's HiLetgo ESP-WROOM-32 ESP32 ESP-32S Development Board.
  WS2812 RGB LED matrix 4x4: WS2812 matrix 4x4
